// Logisim project CPU.circ as structural Verilog: 7 circuits, main circuit main
module HalfSum (
  input  a,
  input  b,
  output CarryOut,
  output Sum
);

  and and_1 (CarryOut, a, b);
  xor xor_1 (Sum, b, a);
endmodule

module main (
  input  in_1,
  input  in_2,
  input  [3:0] in_3,
  input  [15:0] in_4,
  input  [3:0] in_5,
  input  [3:0] in_6,
  output [15:0] out_7
);

  wire clock_1_out;
  wire [15:0] registrador_1_saidab;

  Clock clock_1 (.out(clock_1_out));
  Registrador registrador_1 (
    .Clock(clock_1_out), .Enable(in_1), .Reset(in_2), .AddressA(in_5), .AddressB(in_6), .Data(in_4),
    .SaidaA(out_7), .SaidaB(registrador_1_saidab));
  // Probe on registrador_1_saidab
  ULA ula_1 (.A(out_7), .B(registrador_1_saidab), .\Operação (in_3), .out_4(in_4));
endmodule

module FullSum (
  input  a,
  input  b,
  input  c,
  output Sum,
  output CarryOut
);

  wire halfsum_1_carryout, halfsum_1_sum, halfsum_2_carryout;

  HalfSum halfsum_1 (.a(a), .b(b), .CarryOut(halfsum_1_carryout), .Sum(halfsum_1_sum));
  HalfSum halfsum_2 (.a(c), .b(halfsum_1_sum), .CarryOut(halfsum_2_carryout), .Sum(Sum));
  or or_1 (CarryOut, halfsum_2_carryout, halfsum_1_carryout);
endmodule

module Sum (
  input  [3:0] in_1,
  input  CarryIn,
  input  [3:0] in_3,
  output [4:0] out_4
);

  wire fullsum_1_carryout, fullsum_2_carryout, fullsum_3_carryout;

  // Probe on in_1
  FullSum fullsum_1 (.a(in_3[0]), .b(in_1[0]), .c(CarryIn), .Sum(out_4[0]), .CarryOut(fullsum_1_carryout));
  FullSum fullsum_2 (.a(in_3[1]), .b(in_1[1]), .c(fullsum_1_carryout), .Sum(out_4[1]), .CarryOut(fullsum_2_carryout));
  FullSum fullsum_3 (.a(in_3[2]), .b(in_1[2]), .c(fullsum_2_carryout), .Sum(out_4[2]), .CarryOut(fullsum_3_carryout));
  FullSum fullsum_4 (.a(in_3[3]), .b(in_1[3]), .c(fullsum_3_carryout), .Sum(out_4[3]), .CarryOut(out_4[4]));
  // Probe on in_3
  // Probe on out_4
endmodule

module ULA (
  input  [15:0] A,
  input  [15:0] B,
  input  [3:0] \Operação ,
  output [15:0] out_4
);

  wire [15:0] outAnd, outDiv, outLeftShift, outMult, outNAND, outNOR, outOr, outRightShift, outSub, outSum,
       outXOR;

  Multiplexer #(.select(4), .width(16)) multiplexer_1 (
    .in0(outSum), .in2(outOr), .in4(outMult), .in6(outNAND), .in8(outDiv), .in10(outAnd), .in12(outSub),
    .in13(outRightShift), .in14(outNOR), .in15(outLeftShift), .out(out_4), .sel(\Operação ));  // open: in1, in3, in5, in7, in9, in11, en
  Adder #(.width(16)) adder_1 (.a(A), .b(B), .out(outSum));  // open: cin, cout
  Subtractor #(.width(16)) subtractor_1 (.a(A), .b(B), .out(outSub));  // open: bin, bout
  Multiplier #(.width(16)) multiplier_1 (.a(A), .b(B), .out(outMult));  // open: cin, cout
  Divider #(.width(16)) divider_1 (.a(A), .b(B), .out(outDiv));  // open: upper, rem
  assign outAnd = A & B;  // AND_Gate and_1, 16 bits wide
  assign outOr = A | B;  // OR_Gate or_1, 16 bits wide
  assign outNAND = ~(A & B);  // NAND_Gate nand_1, 16 bits wide
  assign outXOR = A ^ B;  // XOR_Gate xor_1, 16 bits wide
  Shifter #(.width(16)) shifter_1 (.in(A), .\dist (B[3:0]), .out(outLeftShift));
  Shifter #(.width(16), .shift("lr")) shifter_2 (.in(A), .\dist (B[3:0]), .out(outRightShift));
endmodule

module Aula (
  input  Dados,
  input  Set,
  input  Enable,
  input  Parecido_com_Enable,
  input  Dados_2,
  input  Enable_2,
  output out_7,
  output out_8,
  output out_9
);

  wire and_1_out, and_2_out, and_3_out, and_4_out, and_5_out, and_6_out, and_7_out, and_8_out, and_9_out,
       and_10_out, and_11_out, Clock_out, not_1_out, not_2_out, not_4_out, not_5_out, not_6_out, not_8_out,
       not_9_out, not_10_out, not_11_out, not_13_out;

  not not_1 (not_1_out, Set);
  and and_1 (and_1_out, out_8, Parecido_com_Enable);
  and and_2 (and_2_out, Dados_2, Enable_2);
  not not_2 (not_2_out, Dados_2);
  and and_3 (and_3_out, not_1_out, not_4_out);
  not not_3 (out_8, and_3_out);
  not not_4 (not_4_out, and_1_out);
  not not_5 (not_5_out, and_2_out);
  and and_4 (and_4_out, not_5_out, not_8_out);
  and and_5 (and_5_out, Enable_2, not_2_out);
  not not_6 (not_6_out, and_5_out);
  not not_7 (out_9, and_4_out);
  not not_8 (not_8_out, and_6_out);
  and and_6 (and_6_out, out_9, not_6_out);
  Clock Clock (.out(Clock_out));
  and and_7 (and_7_out, Enable, Clock_out);
  not not_9 (not_9_out, Dados);
  and and_8 (and_8_out, Dados, and_7_out);
  not not_10 (not_10_out, and_8_out);
  and and_9 (and_9_out, and_7_out, not_9_out);
  not not_11 (not_11_out, and_9_out);
  not not_12 (out_7, and_10_out);
  and and_10 (and_10_out, not_10_out, not_13_out);
  and and_11 (and_11_out, out_7, not_11_out);
  not not_13 (not_13_out, and_11_out);
endmodule

module Registrador (
  input  Clock,
  input  Enable,
  input  Reset,
  input  [3:0] AddressA,
  input  [3:0] AddressB,
  input  [15:0] Data,
  output [15:0] SaidaA,
  output [15:0] SaidaB
);

  wire SaidaEN1, SaidaEN2, SaidaEN3, SaidaEN4, SaidaEN5, SaidaEN6, SaidaEN7, SaidaEN8, SaidaEN9, SaidaEN10,
       SaidaEN11, SaidaEN12, SaidaEN13, SaidaEN14, SaidaEN15, SaidaEN16;
  wire [15:0] Saida1, Saida2, Saida3, Saida4, Saida5, Saida6, Saida7, Saida8, Saida9, Saida10, Saida11,
       Saida12, Saida13, Saida14, Saida15, Saida16;

  Register #(.width(16)) register_1 (.D(Data), .en(SaidaEN8), .Q(Saida8), .clk(Clock), .clr(Reset));
  Register #(.width(16)) register_2 (.D(Data), .en(SaidaEN9), .Q(Saida9), .clk(Clock), .clr(Reset));
  Register #(.width(16)) register_3 (.D(Data), .en(SaidaEN1), .Q(Saida1), .clk(Clock), .clr(Reset));
  Register #(.width(16)) register_4 (.D(Data), .en(SaidaEN2), .Q(Saida2), .clk(Clock), .clr(Reset));
  Register #(.width(16)) register_5 (.D(Data), .en(SaidaEN3), .Q(Saida3), .clk(Clock), .clr(Reset));
  Register #(.width(16)) register_6 (.D(Data), .en(SaidaEN4), .Q(Saida4), .clk(Clock), .clr(Reset));
  Register #(.width(16)) register_7 (.D(Data), .en(SaidaEN5), .Q(Saida5), .clk(Clock), .clr(Reset));
  Register #(.width(16)) register_8 (.D(Data), .en(SaidaEN15), .Q(Saida15), .clk(Clock), .clr(Reset));
  Register #(.width(16)) register_9 (.D(Data), .en(SaidaEN11), .Q(Saida11), .clk(Clock), .clr(Reset));
  Register #(.width(16)) register_10 (.D(Data), .en(SaidaEN14), .Q(Saida14), .clk(Clock), .clr(Reset));
  Register #(.width(16)) register_11 (.D(Data), .en(SaidaEN16), .Q(Saida16), .clk(Clock), .clr(Reset));
  Register #(.width(16)) register_12 (.D(Data), .en(SaidaEN12), .Q(Saida12), .clk(Clock), .clr(Reset));
  Register #(.width(16)) register_13 (.D(Data), .en(SaidaEN13), .Q(Saida13), .clk(Clock), .clr(Reset));
  Register #(.width(16)) register_14 (.D(Data), .en(SaidaEN6), .Q(Saida6), .clk(Clock), .clr(Reset));
  Register #(.width(16)) register_15 (.D(Data), .en(SaidaEN7), .Q(Saida7), .clk(Clock), .clr(Reset));
  Register #(.width(16)) register_16 (.D(Data), .en(SaidaEN10), .Q(Saida10), .clk(Clock), .clr(Reset));
  Demultiplexer #(.select(4)) demultiplexer_1 (
    .out0(SaidaEN1), .out1(SaidaEN2), .out2(SaidaEN3), .out3(SaidaEN4), .out4(SaidaEN5), .out5(SaidaEN6),
    .out6(SaidaEN7), .out7(SaidaEN8), .out8(SaidaEN9), .out9(SaidaEN10), .out10(SaidaEN11),
    .out11(SaidaEN12), .out12(SaidaEN13), .out13(SaidaEN14), .out14(SaidaEN15), .out15(SaidaEN16),
    .in(Enable), .sel(AddressA));  // open: en
  Multiplexer #(.select(4), .width(16)) multiplexer_1 (
    .in0(Saida1), .in2(Saida2), .in4(Saida3), .in6(Saida4), .in8(Saida5), .in10(Saida6), .in12(Saida7),
    .in14(Saida8), .out(SaidaA), .sel(AddressA));  // open: in1, in3, in5, in7, in9, in11, in13, in15, en
  Multiplexer #(.select(4), .width(16)) multiplexer_2 (
    .in0(Saida9), .in2(Saida10), .in4(Saida11), .in6(Saida12), .in8(Saida13), .in10(Saida14), .in12(Saida15),
    .in14(Saida16), .out(SaidaB), .sel(AddressB));  // open: in1, in3, in5, in7, in9, in11, in13, in15, en
endmodule
