// Logisim project CPU.circ as structural Verilog
module main (
);

  wire button_1_out, clock_1_out;
  wire [11:0] processador_1_nextline;
  wire [15:0] rom_1_data;

  DotMatrix #(.matrixcols(32), .matrixrows(32), .persist(1)) dotmatrix_1 ();  // open: col0, col1, col2, col3, col4, col5, col6, col7, col8, col9, col10, col11, col12, col13, col14, col15, col16, col17, col18, col19, col20, col21, col22, col23, col24, col25, col26, col27, col28, col29, col30, col31
  Clock clock_1 (.out(clock_1_out));
  Button button_1 (.out(button_1_out));
  RAM #(.addrWidth(16), .dataWidth(16), .bus("separate")) ram_1 (
    .clk(clock_1_out), .clr(button_1_out));  // open: addr, din, data, str, sel, ld
  ROM #(.addrWidth(12), .dataWidth(16)) rom_1 (.addr(processador_1_nextline), .data(rom_1_data));  // open: sel
  Joystick joystick_1 ();  // open: x, y
  Processador processador_1 (
    .Inst(rom_1_data), .Clock(clock_1_out), .in_3(button_1_out), .NextLine(processador_1_nextline));
endmodule

module ULA (
  input  [15:0] A,
  input  [15:0] B,
  input  [3:0] Op,
  output [15:0] R,
  output out_5
);

  wire [15:0] And, Complet, LeftShift, Not, Or, OutDiv, OutMul, OutSub, OutSum, RigthShift, Xor;

  Negator #(.width(16)) negator_1 (.in(A), .out(Complet));
  assign And = A & B;  // AND_Gate and_1, 16 bits wide
  assign Or = A | B;  // OR_Gate or_1, 16 bits wide
  assign Not = ~A;  // NOT_Gate not_1, 16 bits wide
  assign Xor = A ^ B;  // XOR_Gate xor_1, 16 bits wide
  Adder #(.width(16)) adder_1 (.a(A), .b(B), .out(OutSum));  // open: cin, cout
  Subtractor #(.width(16)) subtractor_1 (.a(A), .b(B), .out(OutSub));  // open: bin, bout
  Multiplier #(.width(16)) multiplier_1 (.a(A), .b(B), .out(OutMul));  // open: cin, cout
  Divider #(.width(16)) divider_1 (.a(A), .b(B), .out(OutDiv));  // open: upper, rem
  Shifter #(.width(16)) shifter_1 (.in(A), .\dist (B[3:0]), .out(LeftShift));
  Shifter #(.width(16), .shift("lr")) shifter_2 (.in(A), .\dist (B[3:0]), .out(RigthShift));
  Comparator #(.width(16)) comparator_1 (.a(A), .b(B), .gt(out_5));  // open: eq, lt
  Multiplexer #(.select(4), .width(16)) multiplexer_1 (
    .in0(OutSum), .in1(OutSub), .in2(OutMul), .in3(OutDiv), .in4(LeftShift), .in5(RigthShift), .in6(Complet),
    .in7(And), .in8(Or), .in9(Not), .in10(Xor), .out(R), .sel(Op));  // open: in11, in12, in13, in14, in15, en
endmodule

module LatchSR (
  input  Set,
  input  Reset,
  output out_3
);

  wire and_1_out, and_2_out, not_2_out;

  and and_1 (and_1_out, Set, not_2_out);
  and and_2 (and_2_out, out_3, Reset);
  not not_1 (out_3, and_1_out);
  not not_2 (not_2_out, and_2_out);
endmodule

module LatchD (
  input  D,
  input  Enable,
  output out_3
);

  wire and_1_out, and_2_out, not_1_out, not_2_out, not_3_out;

  not not_1 (not_1_out, D);
  and and_1 (and_1_out, D, Enable);
  not not_2 (not_2_out, and_1_out);
  and and_2 (and_2_out, Enable, not_1_out);
  not not_3 (not_3_out, and_2_out);
  LatchSR latchsr_1 (.Set(not_2_out), .Reset(not_3_out), .out_3(out_3));
endmodule

module FlipFlop (
  input  D,
  input  Enable,
  input  Clock,
  output out_4
);

  wire and_1_out, latchd_1_out_3, not_1_out;

  and and_1 (and_1_out, Enable, Clock);
  not not_1 (not_1_out, Clock);
  LatchD latchd_1 (.D(D), .Enable(and_1_out), .out_3(latchd_1_out_3));
  LatchD latchd_2 (.D(latchd_1_out_3), .Enable(not_1_out), .out_3(out_4));
endmodule

module Reg (
  input  Clock,
  input  Enable,
  input  Reset,
  input  [3:0] AddresA,
  input  [3:0] AddresB,
  input  [15:0] Data,
  output [15:0] DataA,
  output [15:0] DataB
);

  wire en0, en1, en2, en3, en4, en5, en6, en7, en8, en9, en10, en11, en12, en13, en14, en15;
  wire [15:0] out0, out1, out2, out3, out4, out5, out6, out7, out8, out9, out10, out11, out12, out13, out14,
       out15;

  Demultiplexer #(.select(4)) demultiplexer_1 (
    .out0(en0), .out1(en1), .out2(en2), .out3(en3), .out4(en4), .out5(en5), .out6(en6), .out7(en7),
    .out8(en8), .out9(en9), .out10(en10), .out11(en11), .out12(en12), .out13(en13), .out14(en14),
    .out15(en15), .in(Enable), .sel(AddresA));  // open: en
  Register #(.width(16)) register_1 (.D(Data), .en(en0), .Q(out0), .clk(Clock), .clr(Reset));
  Register #(.width(16)) register_2 (.D(Data), .en(en1), .Q(out1), .clk(Clock), .clr(Reset));
  Register #(.width(16)) register_3 (.D(Data), .en(en3), .Q(out3), .clk(Clock), .clr(Reset));
  Register #(.width(16)) register_4 (.D(Data), .en(en4), .Q(out4), .clk(Clock), .clr(Reset));
  Register #(.width(16)) register_5 (.D(Data), .en(en5), .Q(out5), .clk(Clock), .clr(Reset));
  Register #(.width(16)) register_6 (.D(Data), .en(en6), .Q(out6), .clk(Clock), .clr(Reset));
  Register #(.width(16)) register_7 (.D(Data), .en(en7), .Q(out7), .clk(Clock), .clr(Reset));
  Register #(.width(16)) register_8 (.D(Data), .en(en8), .Q(out8), .clk(Clock), .clr(Reset));
  Multiplexer #(.select(4), .width(16)) multiplexer_1 (
    .in0(out0), .in1(out1), .in2(out2), .in3(out3), .in4(out4), .in5(out5), .in6(out6), .in7(out7),
    .in8(out8), .in9(out9), .in10(out10), .in11(out11), .in12(out12), .in13(out13), .in14(out14),
    .in15(out15), .out(DataA), .sel(AddresA));  // open: en
  Multiplexer #(.select(4), .width(16)) multiplexer_2 (
    .in0(out0), .in1(out1), .in2(out2), .in3(out3), .in4(out4), .in5(out5), .in6(out6), .in7(out7),
    .in8(out8), .in9(out9), .in10(out10), .in11(out11), .in12(out12), .in13(out13), .in14(out14),
    .in15(out15), .out(DataB), .sel(AddresB));  // open: en
  Register #(.width(16)) register_9 (.D(Data), .en(en9), .Q(out9), .clk(Clock), .clr(Reset));
  Register #(.width(16)) register_10 (.D(Data), .en(en10), .Q(out10), .clk(Clock), .clr(Reset));
  Register #(.width(16)) register_11 (.D(Data), .en(en11), .Q(out11), .clk(Clock), .clr(Reset));
  Register #(.width(16)) register_12 (.D(Data), .en(en12), .Q(out12), .clk(Clock), .clr(Reset));
  Register #(.width(16)) register_13 (.D(Data), .en(en15), .Q(out15), .clk(Clock), .clr(Reset));
  Register #(.width(16)) register_14 (.D(Data), .en(en2), .Q(out2), .clk(Clock), .clr(Reset));
  Register #(.width(16)) register_15 (.D(Data), .en(en13), .Q(out13), .clk(Clock), .clr(Reset));
  Register #(.width(16)) register_16 (.D(Data), .en(en14), .Q(out14), .clk(Clock), .clr(Reset));

  // Other names for the same wires on the sheet: addA[3:0] = AddresA; addB[3:0] = AddresB; clk = Clock; en = Enable;
  //   rst = Reset
endmodule

module Processador (
  input  [15:0] Inst,
  input  Clock,
  input  in_3,
  output [11:0] NextLine
);

  wire ismov, isop, not_1_out, not_2_out, not_3_out, not_4_out, not_5_out, not_6_out, regen;
  wire [3:0] a;
  wire [11:0] next;
  wire [15:0] data, reg_1_dataa, reg_1_datab, ulaout;

  Register #(.width(12)) PC (.D(next), .Q(NextLine), .clk(Clock), .clr(in_3));  // open: en
  and and_1 (isop, Inst[12], not_1_out, not_2_out, not_3_out);
  not not_1 (not_1_out, Inst[13]);
  not not_2 (not_2_out, Inst[14]);
  not not_3 (not_3_out, Inst[15]);
  Adder #(.width(12)) adder_1 (.a(NextLine), .b(12'h1), .out(next));  // open: cin, cout
  not not_4 (not_4_out, Inst[12]);
  and and_2 (ismov, not_4_out, Inst[13], not_5_out, not_6_out);
  not not_5 (not_5_out, Inst[14]);
  not not_6 (not_6_out, Inst[15]);
  Reg reg_1 (
    .Clock(Clock), .Enable(regen), .Reset(in_3), .AddresA(a), .AddresB(Inst[3:0]), .Data(data),
    .DataA(reg_1_dataa), .DataB(reg_1_datab));
  // Probe on reg_1_dataa
  // Probe on reg_1_datab
  or or_1 (regen, isop, ismov);
  // Probe on ulaout
  ULA ula_1 (.A(reg_1_dataa), .B(reg_1_datab), .R(ulaout), .Op(Inst[11:8]));  // open: out_5
  // Probe on data
  Multiplexer #(.width(16)) multiplexer_1 (
    .in0(ulaout), .in1({{8{1'b0}}, Inst[7:0]}), .out(data), .sel(ismov));  // open: en
  Multiplexer #(.width(4)) multiplexer_2 (.in0(Inst[7:4]), .in1(Inst[11:8]), .out(a), .sel(ismov));  // open: en

  // Other names for the same wires on the sheet: b[3:0] = Inst[3:0]; c[7:0] = Inst[7:0]; s0[3:0] = Inst[3:0];
  //   s1[3:0] = Inst[7:4]; clk = Clock; crr[11:0] = NextLine; p[3:0] = Inst[11:8]; s2[3:0] = Inst[11:8];
  //   s3[3:0] = Inst[15:12]; rst = in_3
endmodule
